// Logisim project LogicLogisim.circ as structural Verilog: 7 circuits, main circuit main
module main (
  input  X3,
  input  X2,
  input  X1
);

  wire DurumD_a, DurumD_b, DurumD_c, Kontol_D_a1k, Kontol_D_a1s, Kontol_D_a1y, Kontol_D_a2k, Kontol_D_a2s,
       Kontol_D_a2y, Kontol_D_a3k, Kontol_D_a3s, Kontol_D_a3y, Kontol_D_at, Kontol_D_bt, Kontol_D_ct;

  DurumDevresi DurumD (.At(Kontol_D_at), .Bt(Kontol_D_bt), .Ct(Kontol_D_ct), .A(DurumD_a), .B(DurumD_b), .C(DurumD_c));
  KontrolDevresi Kontol_D (
    .X3(X3), .X2(X2), .X1(X1), .A(DurumD_a), .B(DurumD_b), .C(DurumD_c), .At(Kontol_D_at), .Bt(Kontol_D_bt),
    .Ct(Kontol_D_ct), .A1K(Kontol_D_a1k), .A1S(Kontol_D_a1s), .A1Y(Kontol_D_a1y), .A2K(Kontol_D_a2k),
    .A2S(Kontol_D_a2s), .A2Y(Kontol_D_a2y), .A3K(Kontol_D_a3k), .A3S(Kontol_D_a3s), .A3Y(Kontol_D_a3y));
  LED A3K (.in(Kontol_D_a3k));
  LED A3S (.in(Kontol_D_a3s));
  LED A1S (.in(Kontol_D_a1s));
  LED A1K (.in(Kontol_D_a1k));
  LED A1Y (.in(Kontol_D_a1y));
  LED A3Y (.in(Kontol_D_a3y));
  LED A2K (.in(Kontol_D_a2k));
  LED A2S (.in(Kontol_D_a2s));
  LED A2Y (.in(Kontol_D_a2y));
endmodule

module JAKA (
  input  X3,
  input  X2,
  input  X1,
  input  A,
  output JA,
  output KA
);

  wire not_1_out, not_2_out, not_3_out;

  not not_1 (not_1_out, X3);
  not not_2 (not_2_out, X2);
  and and_1 (JA, not_1_out, not_2_out, not_3_out);
  not not_3 (not_3_out, X1);
  or or_1 (KA, X1, X2, X3);
endmodule

module JBKB (
  input  X3,
  input  X2,
  input  X1,
  input  B,
  output JB,
  output KB
);

  wire and_1_out;

  not not_1 (JB, X1);
  and and_1 (and_1_out, X3, X2);
  or or_1 (KB, X1, and_1_out);
endmodule

module JCKC (
  input  X3,
  input  X2,
  input  X1,
  input  C,
  output JC,
  output KC
);

  wire and_1_out, not_1_out;

  not not_1 (not_1_out, X2);
  or or_1 (JC, not_1_out, X1);
  and and_1 (and_1_out, X3, X1);
  or or_2 (KC, X2, and_1_out);
endmodule

module At (
  input  X3,
  input  X2,
  input  X1,
  input  A,
  input  B,
  input  C,
  output At
);

  wire and_1_out, and_2_out, and_3_out, and_4_out, and_5_out, not_1_out, not_2_out, not_3_out, not_4_out,
       not_5_out, not_6_out, not_7_out, not_8_out, not_9_out;

  not not_1 (not_1_out, X3);
  not not_2 (not_2_out, X2);
  not not_3 (not_3_out, X1);
  not not_4 (not_4_out, A);
  not not_5 (not_5_out, B);
  not not_6 (not_6_out, A);
  not not_7 (not_7_out, C);
  not not_8 (not_8_out, A);
  not not_9 (not_9_out, A);
  and and_1 (and_1_out, not_1_out, not_2_out, not_3_out);
  and and_2 (and_2_out, X2, X1, not_4_out, not_5_out, C);
  and and_3 (and_3_out, X2, X1, not_6_out, B, not_7_out);
  and and_4 (and_4_out, X3, X1, not_8_out, C);
  and and_5 (and_5_out, X3, X2, not_9_out, B);
  or or_1 (At, and_1_out, and_2_out, and_3_out, and_4_out, and_5_out);
endmodule

module DurumDevresi (
  input  At,
  input  Bt,
  input  Ct,
  output A,
  output B,
  output C
);

  wire clock_1_out;

  Clock clock_1 (.out(clock_1_out));
  D_Flip_Flop d_ff_1 (.clk(clock_1_out), .D(At), .Q(A));  // open: Qn, preset, en, reset
  D_Flip_Flop d_ff_2 (.clk(clock_1_out), .D(Bt), .Q(B));  // open: Qn, preset, en, reset
  D_Flip_Flop d_ff_3 (.clk(clock_1_out), .D(Ct), .Q(C));  // open: Qn, preset, en, reset
endmodule

module KontrolDevresi (
  input  X3,
  input  X2,
  input  X1,
  input  A,
  input  B,
  input  C,
  output At,
  output Bt,
  output Ct,
  output A1K,
  output A1S,
  output A1Y,
  output A2K,
  output A2S,
  output A2Y,
  output A3K,
  output A3S,
  output A3Y
);

  wire and_1_out, and_2_out, and_3_out, and_4_out, and_5_out, and_6_out, and_7_out, and_8_out, and_9_out,
       and_10_out, and_11_out, and_12_out, and_13_out, and_14_out, and_15_out, and_16_out, and_17_out,
       and_18_out, and_19_out, and_20_out, and_21_out, and_22_out, and_23_out, and_24_out, and_25_out,
       and_26_out, and_27_out, and_28_out, and_29_out, and_30_out, and_31_out, and_32_out, and_33_out,
       and_34_out, and_35_out, and_36_out, and_37_out, and_38_out, and_39_out, and_40_out, and_41_out,
       and_42_out, and_43_out, and_44_out, and_45_out, and_46_out, and_47_out, and_48_out, and_49_out,
       and_50_out, and_51_out, and_52_out, and_53_out, and_54_out, and_55_out, and_56_out, and_57_out,
       and_58_out, not_1_out, not_2_out, not_3_out, not_4_out, not_5_out, not_6_out, not_7_out, not_8_out,
       not_9_out, not_10_out, not_11_out, not_12_out, not_13_out, not_14_out, not_15_out, not_16_out,
       not_17_out, not_18_out, not_19_out, not_20_out, not_21_out, not_22_out, not_23_out, not_24_out,
       not_25_out, not_26_out, not_27_out, not_28_out, not_29_out, not_30_out, not_31_out, not_32_out,
       not_33_out, not_34_out, not_35_out, not_36_out, not_37_out, not_38_out, not_39_out, not_40_out,
       not_41_out, not_42_out, not_43_out, not_44_out, not_45_out, not_46_out, not_47_out, not_48_out,
       not_49_out, not_50_out, not_51_out, not_52_out, not_53_out, not_54_out, not_55_out, not_56_out,
       not_57_out, not_58_out, not_59_out, not_60_out, not_61_out, not_62_out, not_63_out, not_64_out,
       not_65_out, not_66_out, not_67_out, not_68_out, not_69_out, not_70_out, not_71_out, not_72_out,
       not_73_out, not_74_out, not_75_out, not_76_out, not_77_out, not_78_out, not_79_out, not_80_out,
       not_81_out, not_82_out, not_83_out, not_84_out, not_85_out, not_86_out, not_87_out, not_88_out,
       not_89_out, not_90_out, not_91_out, not_92_out;

  not not_1 (not_1_out, X3);
  not not_2 (not_2_out, X2);
  not not_3 (not_3_out, X1);
  not not_4 (not_4_out, A);
  not not_5 (not_5_out, B);
  not not_6 (not_6_out, A);
  not not_7 (not_7_out, C);
  not not_8 (not_8_out, A);
  not not_9 (not_9_out, A);
  not not_10 (not_10_out, X3);
  not not_11 (not_11_out, X1);
  not not_12 (not_12_out, X2);
  not not_13 (not_13_out, X1);
  not not_14 (not_14_out, X1);
  not not_15 (not_15_out, B);
  not not_16 (not_16_out, X1);
  not not_17 (not_17_out, B);
  not not_18 (not_18_out, C);
  not not_19 (not_19_out, A);
  not not_20 (not_20_out, B);
  not not_21 (not_21_out, C);
  not not_22 (not_22_out, B);
  not not_23 (not_23_out, X3);
  not not_24 (not_24_out, X2);
  not not_25 (not_25_out, X2);
  not not_26 (not_26_out, X1);
  not not_27 (not_27_out, X2);
  not not_28 (not_28_out, C);
  not not_29 (not_29_out, A);
  not not_30 (not_30_out, C);
  not not_31 (not_31_out, X3);
  not not_32 (not_32_out, C);
  not not_33 (not_33_out, A);
  not not_34 (not_34_out, C);
  not not_35 (not_35_out, B);
  not not_36 (not_36_out, A);
  not not_37 (not_37_out, C);
  not not_38 (not_38_out, B);
  not not_39 (not_39_out, C);
  not not_40 (not_40_out, A);
  not not_41 (not_41_out, B);
  not not_42 (not_42_out, C);
  not not_43 (not_43_out, B);
  not not_44 (not_44_out, A);
  not not_45 (not_45_out, B);
  not not_46 (not_46_out, A);
  not not_47 (not_47_out, B);
  not not_48 (not_48_out, X3);
  not not_49 (not_49_out, X2);
  not not_50 (not_50_out, X2);
  not not_51 (not_51_out, A);
  not not_52 (not_52_out, C);
  not not_53 (not_53_out, A);
  not not_54 (not_54_out, B);
  not not_55 (not_55_out, C);
  not not_56 (not_56_out, X3);
  not not_57 (not_57_out, X3);
  not not_58 (not_58_out, X2);
  not not_59 (not_59_out, A);
  not not_60 (not_60_out, B);
  not not_61 (not_61_out, A);
  not not_62 (not_62_out, B);
  not not_63 (not_63_out, A);
  not not_64 (not_64_out, C);
  not not_65 (not_65_out, A);
  not not_66 (not_66_out, C);
  not not_67 (not_67_out, X3);
  not not_68 (not_68_out, X1);
  not not_69 (not_69_out, X1);
  not not_70 (not_70_out, A);
  not not_71 (not_71_out, B);
  not not_72 (not_72_out, B);
  not not_73 (not_73_out, C);
  not not_74 (not_74_out, X1);
  not not_75 (not_75_out, A);
  not not_76 (not_76_out, B);
  not not_77 (not_77_out, C);
  not not_78 (not_78_out, X2);
  not not_79 (not_79_out, A);
  not not_80 (not_80_out, B);
  not not_81 (not_81_out, C);
  not not_82 (not_82_out, A);
  not not_83 (not_83_out, A);
  not not_84 (not_84_out, X2);
  not not_85 (not_85_out, X1);
  not not_86 (not_86_out, X2);
  not not_87 (not_87_out, B);
  not not_88 (not_88_out, C);
  not not_89 (not_89_out, B);
  and and_1 (and_1_out, not_1_out, not_2_out, not_3_out);
  and and_2 (and_2_out, X2, X1, not_4_out, not_5_out, C);
  and and_3 (and_3_out, X2, X1, not_6_out, B, not_7_out);
  and and_4 (and_4_out, X3, X1, not_8_out, C);
  and and_5 (and_5_out, X3, X2, not_9_out, B);
  and and_6 (and_6_out, not_10_out, not_11_out);
  and and_7 (and_7_out, not_12_out, not_13_out);
  and and_8 (and_8_out, not_14_out, not_15_out);
  and and_9 (and_9_out, not_16_out, A);
  and and_10 (and_10_out, X2, A, not_17_out, not_18_out);
  and and_11 (and_11_out, X3, not_19_out, B, C);
  and and_12 (and_12_out, X3, A, not_20_out, not_21_out);
  and and_13 (and_13_out, X3, X2, A, not_22_out);
  and and_14 (and_14_out, not_23_out, not_24_out);
  and and_15 (and_15_out, not_25_out, not_26_out);
  and and_16 (and_16_out, not_27_out, not_28_out);
  and and_17 (and_17_out, X1, not_29_out, not_30_out);
  and and_18 (and_18_out, not_31_out, X1, B);
  and and_19 (and_19_out, X1, B, not_32_out);
  and and_20 (and_20_out, X1, A, C);
  and and_21 (and_21_out, X3, not_33_out, B, not_34_out);
  and and_22 (and_22_out, X3, A, not_35_out, C);
  not not_90 (not_90_out, X1);
  and and_23 (and_23_out, X2, not_36_out, B, not_37_out);
  and and_24 (and_24_out, X2, A, not_38_out, not_39_out);
  and and_25 (and_25_out, X3, not_40_out, B, C);
  and and_26 (and_26_out, X3, A, not_41_out, not_42_out);
  and and_27 (and_27_out, X3, X2, A, not_43_out);
  and and_28 (and_28_out, X2, X1, not_44_out, not_45_out, C);
  and and_29 (and_29_out, X3, X1, not_46_out, not_47_out, C);
  and and_30 (and_30_out, not_48_out, not_49_out, X1);
  and and_31 (and_31_out, not_50_out, X1, not_51_out, not_52_out);
  and and_32 (and_32_out, X1, not_53_out, not_54_out, not_55_out);
  and and_33 (and_33_out, not_56_out, X1, B, C);
  and and_34 (and_34_out, not_57_out, X1, A, C);
  and and_35 (and_35_out, not_58_out, X1, A, C);
  and and_36 (and_36_out, X1, A, B);
  not not_91 (not_91_out, X2);
  and and_37 (and_37_out, X1, not_59_out, not_60_out);
  and and_38 (and_38_out, X1, C);
  and and_39 (and_39_out, X1, A, B);
  and and_40 (and_40_out, X3, not_61_out, B, C);
  and and_41 (and_41_out, X3, A, not_62_out, C);
  and and_42 (and_42_out, X2, X1, not_63_out, B, not_64_out);
  and and_43 (and_43_out, X3, X2, not_65_out, B, not_66_out);
  and and_44 (and_44_out, not_67_out, X2, not_68_out);
  and and_45 (and_45_out, X2, not_69_out, not_70_out, not_71_out);
  and and_46 (and_46_out, X2, A, not_72_out, not_73_out);
  and and_47 (and_47_out, X2, not_74_out, A, B);
  not not_92 (not_92_out, X3);
  and and_48 (and_48_out, X1, not_75_out, not_76_out);
  and and_49 (and_49_out, X1, B, not_77_out);
  and and_50 (and_50_out, not_78_out, X1, A, C);
  and and_51 (and_51_out, X2, not_79_out, not_80_out);
  and and_52 (and_52_out, X2, not_81_out);
  and and_53 (and_53_out, X2, A, B);
  and and_54 (and_54_out, X3, X1, not_82_out, B, C);
  and and_55 (and_55_out, X3, X2, not_83_out, B, C);
  and and_56 (and_56_out, X3, not_84_out, not_85_out);
  and and_57 (and_57_out, X3, not_86_out, A, not_87_out, not_88_out);
  and and_58 (and_58_out, X3, X2, A, not_89_out, C);
  or or_1 (At, and_1_out, and_2_out, and_3_out, and_4_out, and_5_out);
  or or_2 (Bt, and_6_out, and_7_out, and_8_out, and_9_out, and_10_out, and_11_out, and_12_out, and_13_out);
  or or_3 (Ct, and_14_out, and_15_out, and_16_out, and_17_out, and_18_out, and_19_out, and_20_out, and_21_out, and_22_out);
  or or_4 (A1K, not_90_out, and_23_out, and_24_out, and_25_out, and_26_out, and_27_out);
  or or_5 (A1S, and_28_out, and_29_out);
  or or_6 (A1Y, and_30_out, and_31_out, and_32_out, and_33_out, and_34_out, and_35_out, and_36_out);
  or or_7 (A2K, not_91_out, and_37_out, and_38_out, and_39_out, and_40_out, and_41_out);
  or or_8 (A2S, and_42_out, and_43_out);
  or or_9 (A2Y, and_44_out, and_45_out, and_46_out, and_47_out);
  or or_10 (A3K, not_92_out, and_48_out, and_49_out, and_50_out, and_51_out, and_52_out, and_53_out);
  or or_11 (A3S, and_54_out, and_55_out);
  or or_12 (A3Y, and_56_out, and_57_out, and_58_out);
endmodule
